# Fritzing sketch esp8266_Neopixel_PIR_Halloween (saved by Fritzing 0.9.3b)
breadboards: 1

parts:
  Bauteil1 = 12 NeoPixel Ring [part_number=1643]  # not connected
  DFRobot_DFPlayer_Mini1 = DFRobot DFPlayer Mini [part_number=DFR0299]
  WeMos_D1_Mini1 = WeMos D1 Mini  # not connected
  C1 = Electrolytic Capacitor [capacitance=47µF voltage=35V package="100 mil [THT, electrolytic]"]  # not connected
  Stromversorgung_Beradboard1 = Stromversorgung Beradboard [package=THT]  # not connected
  SPKR1 = Loudspeaker  # not connected
  DFRobot_DFPlayer_Mini2 = DFRobot DFPlayer Mini [part_number=DFR0299]  # not connected
  YwRobot_Power_Supply1 = YwRobot Breadboard Power Supply [part_number=545043]  # not connected

nets:
  N1: DFRobot_DFPlayer_Mini1.GND-1, DFRobot_DFPlayer_Mini1.GND-2

notes:
  Voltage Supply:
  2x 3.3V

custom parts:
  12 NeoPixel Ring: 12 ultra bright smart LED NeoPixels are arranged in a circle with 1.5" (37mm) outer diameter. The rings are 'chainable' - connect the output pin of one to the input pin of another. Use only one microcontroller pin to control as many as you can chain together! Each LED is addressable as the driver chip is inside the LED. Each one has ~18mA constant current drive so the color will be very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
  WeMos D1 Mini: The D1 mini is a mini wifi board based on ESP-8266EX.
  YwRobot Breadboard Power Supply: The YwRobot Breadboard Power Supply (MB-V2) has two power rails; they can be 5V or 3V3. Power to the module can be provided through the female USB socket or through the A10 (female) 2.1mm power jack.
